// Logisim project ULA.circ as structural Verilog: 4 circuits, main circuit main
module main (
  input  in_1,
  input  [2:0] in_2,
  input  [2:0] in_3
);

  wire somador_completo_1_carry, somador_completo_2_carry, subtrador_completo_1_bout,
       subtrador_completo_2_bout;
  wire [3:0] somador_completo_1_r, subtrador_completo_1_r;

  somador_completo somador_completo_1 (
    .C(in_1), .A(in_2[0]), .B(in_3[0]), .R(somador_completo_1_r[0]), .Carry(somador_completo_1_carry));
  somador_completo somador_completo_2 (
    .C(somador_completo_1_carry), .A(in_2[1]), .B(in_3[1]), .R(somador_completo_1_r[1]),
    .Carry(somador_completo_2_carry));
  somador_completo somador_completo_3 (
    .C(somador_completo_2_carry), .A(in_2[2]), .B(in_3[2]), .R(somador_completo_1_r[2]),
    .Carry(somador_completo_1_r[3]));
  subtrador_completo subtrador_completo_1 (
    .Bin(in_1), .A(in_2[0]), .B(in_3[0]), .R(subtrador_completo_1_r[0]), .Bout(subtrador_completo_1_bout));
  subtrador_completo subtrador_completo_2 (
    .Bin(subtrador_completo_1_bout), .A(in_2[1]), .B(in_3[1]), .R(subtrador_completo_1_r[1]),
    .Bout(subtrador_completo_2_bout));
  subtrador_completo subtrador_completo_3 (
    .Bin(subtrador_completo_2_bout), .A(in_2[2]), .B(in_3[2]), .R(subtrador_completo_1_r[2]),
    .Bout(subtrador_completo_1_r[3]));
  Hex_Digit_Display hex_digit_display_1 (.value(somador_completo_1_r));  // open: dp
  Hex_Digit_Display hex_digit_display_2 (.value(subtrador_completo_1_r));  // open: dp
endmodule

module somador_completo (
  input  C,
  input  A,
  input  B,
  output R,
  output Carry
);

  wire and_1_out, and_2_out, xor_1_out, xor_2_out;

  xor xor_1 (xor_1_out, A, B);
  xor xor_2 (xor_2_out, A, B);
  xor xor_3 (R, xor_1_out, C);
  and and_1 (and_1_out, xor_2_out, C);
  or or_1 (Carry, and_1_out, and_2_out);
  and and_2 (and_2_out, A, B);
endmodule

module subtrador_completo (
  input  Bin,
  input  A,
  input  B,
  output R,
  output Bout
);

  wire and_1_out, and_2_out, not_1_out, xor_1_out, xor_3_out;

  xor xor_1 (xor_1_out, A, B);
  xor xor_2 (R, xor_1_out, Bin);
  xor xor_3 (xor_3_out, B, Bin);
  and and_1 (and_1_out, xor_3_out, not_1_out);
  not not_1 (not_1_out, A);
  and and_2 (and_2_out, B, Bin);
  or or_1 (Bout, and_1_out, and_2_out);
endmodule

module teste (
  input  A,
  input  B,
  input  C,
  output R,
  output out_5
);

  wire and_1_out, and_2_out, not_1_out, xor_1_out, xor_3_out;

  xor xor_1 (xor_1_out, A, B);
  xor xor_2 (R, xor_1_out, C);
  xor xor_3 (xor_3_out, B, C);
  not not_1 (not_1_out, A);
  and and_1 (and_1_out, B, C);
  and and_2 (and_2_out, xor_3_out, not_1_out);
  or or_1 (out_5, and_2_out, and_1_out);
endmodule
